# Fritzing sketch schematic (saved by Fritzing 0.8.5b)
circuit board: 5.36311cm x 6.88566cm
breadboards: 1

parts:
  Arduino_Uno = Arduino Uno (Rev3)
  Part2 = SRF05 Ultrasonic Rangefinder
  J1 = Piezo Speaker
  Raspberry_Pi_B_rev1 = Raspberry Pi B rev2  # not connected

nets:
  N1: Arduino_Uno.D11_PWM/MOSI, J1.pin2
  N2: Arduino_Uno.D12/MISO, Part2.Echo
  N3: Arduino_Uno.D13/SCK, Part2.Trig
  GND: Arduino_Uno.GND, Part2.GND, J1.pin1
  5V: Arduino_Uno.5V, Part2.VCC
